# Fritzing sketch full_decoder_pcb_v3_1 (saved by Fritzing 0.9.3b)
circuit board: 11.836cm x 6.3144cm

parts:
  HCTL = DIP - 16 pins [chip_label=HCTL-2017-A00 package="DIP (Dual Inline) [THT]"]
  PUp1_10k = Resistor [tolerance=±5% resistance=10k package=THT]
  100pF = Ceramic Capacitor [capacitance=0.1nF package="100 mil [THT, multilayer]"]
  PUp2_10k = Resistor [tolerance=±5% resistance=10k package=THT]
  PUp3_10k = Resistor [tolerance=±5% resistance=10k package=THT]
  J1 = screw terminal, 8 pins
  PUp4 = Resistor [tolerance=±5% resistance=120 package=THT]
  SN75115 = IC, DIP package, 16 pins [chip_label=SN75115]
  1µF = Electrolytic Capacitor [capacitance=1µF package="100 mil [THT, electrolytic]"]
  10pF = Ceramic Capacitor [capacitance=10pF package="100 mil [THT, multilayer]"]
  300Ω = Resistor [tolerance=±5% resistance=300 package=THT]
  300Ω_2 = Resistor [tolerance=±5% resistance=300 package=THT]
  B_OUT = female pin header, 2 pins [form="♀ (female)"]
  A_OUT = female pin header, 2 pins [form="♀ (female)"]
  10pF_2 = Ceramic Capacitor [capacitance=10pF package="100 mil [THT, multilayer]"]
  DRIVER = IC, DIP package, 20 pins [chip_label=SN74HCT541N]
  100pF_2 = Ceramic Capacitor [capacitance=0.1nF package="100 mil [THT, multilayer]"]
  100pF_3 = Ceramic Capacitor [capacitance=0.1nF package="100 mil [THT, multilayer]"]
  1µF_2 = Electrolytic Capacitor [capacitance=1µF package="100 mil [THT, electrolytic]"]
  10kΩ = Resistor [tolerance=±5% resistance=10k package=THT]
  10kΩ_2 = Resistor [tolerance=±5% resistance=10k package=THT]
  STAT_LED1 = Screw terminal - 2 pins [package=THT]
  80Ω = Resistor [tolerance=±5% resistance=80 package=THT]
  80Ω_2 = Resistor [tolerance=±5% resistance=80 package=THT]
  STAT_LED2 = Screw terminal - 2 pins [package=THT]
  80Ω_3 = Resistor [tolerance=±5% resistance=80 package=THT]
  STAT_LED3 = Screw terminal - 2 pins [package=THT]
  80Ω_4 = Resistor [tolerance=±5% resistance=80 package=THT]
  STAT_LED4 = Screw terminal - 2 pins [package=THT]
  J2 = female pin header, 9 pins [form="♀ (female)"]
  A9 = Screw terminal - 2 pins [package=THT]
  A8 = Screw terminal - 2 pins [package=THT]
  A3 = Screw terminal - 2 pins [package=THT]
  A2 = Screw terminal - 2 pins [package=THT]
  TRIG1 = Screw terminal - 2 pins [package=THT]
  TRIG2 = Screw terminal - 2 pins [package=THT]
  TRIG3 = Screw terminal - 2 pins [package=THT]
  100pF_4 = Ceramic Capacitor [capacitance=0.1nF package="100 mil [THT, multilayer]"]
  Teensy1 = Teensy 3.6 (Basic)
  HCTL_RESET = Pushbutton [package="[THT]"]
  CNT_RESET = Pushbutton [package="[THT]"]

nets:
  N1: HCTL.D0, Teensy1.D2
  N2: HCTL.CLK, DRIVER.pin11, 100pF_3.0
  N3: HCTL.SEL, PUp1_10k.Pin_0, 100pF.0, DRIVER.pin14
  N4: HCTL.OE, PUp2_10k.Pin_0, DRIVER.pin13, 100pF_2.0
  N5: HCTL.RST, PUp3_10k.Pin_0, DRIVER.pin12, 100pF_4.0
  N6: HCTL.CH_B, SN75115.pin1, SN75115.pin2, 300Ω.Pin_1, A_OUT.pin1
  N7: HCTL.CH_A, SN75115.pin14, SN75115.pin15, 300Ω_2.Pin_1, B_OUT.pin1
  GND: HCTL.GND, 100pF.1, J1.pin3, SN75115.pin8, 1µF.-, 10pF.0, B_OUT.pin2, A_OUT.pin2, 10pF_2.0, DRIVER.pin1, DRIVER.pin10, DRIVER.pin19, 100pF_2.1, 100pF_3.1, 1µF_2.-, STAT_LED1.pin1, STAT_LED2.pin1, STAT_LED3.pin1, STAT_LED4.pin1, A9.pin1, A8.pin1, A3.pin1, A2.pin1, TRIG1.pin1, TRIG2.pin1, TRIG3.pin1, 100pF_4.1, Teensy1.GND#0, Teensy1.AGND, Teensy1.GND#55, HCTL_RESET.Pin_1, HCTL_RESET.Pin_2, CNT_RESET.Pin_1, CNT_RESET.Pin_2
  N8: HCTL.D7, Teensy1.D5
  N9: HCTL.D6, Teensy1.A7/D21
  N10: HCTL.D5, Teensy1.A6/D20
  N11: HCTL.D4, Teensy1.D6
  N12: HCTL.D3, Teensy1.D8
  N13: HCTL.D2, Teensy1.D7
  N14: HCTL.D1, Teensy1.A0/D14
  5V: HCTL.VDD, PUp1_10k.Pin_1, PUp2_10k.Pin_1, PUp3_10k.Pin_1, J1.pin8, SN75115.pin3, SN75115.pin13, SN75115.pin16, 1µF.+, 300Ω.Pin_0, 300Ω_2.Pin_0, DRIVER.pin20, 1µF_2.+, 10kΩ.Pin_1, 10kΩ_2.Pin_1, Teensy1.Vin
  N15: J1.pin1, SN75115.pin6
  N16: J1.pin2, SN75115.pin7
  N17: J1.pin4, SN75115.pin10
  N18: J1.pin5, SN75115.pin9
  N19: J1.pin6, PUp4.Pin_0
  N20: J1.pin7, PUp4.Pin_1
  N21: SN75115.pin4, 10pF.1
  N22: SN75115.pin12, 10pF_2.1
  N23: DRIVER.pin2, Teensy1.A5/D19
  N24: DRIVER.pin3, Teensy1.A4/D18
  N25: DRIVER.pin4, Teensy1.A1/D15
  N26: DRIVER.pin6, Teensy1.D24
  N27: DRIVER.pin7, Teensy1.D12
  N28: DRIVER.pin8, Teensy1.D11
  N29: DRIVER.pin9, Teensy1.D10
  N30: DRIVER.pin16, TRIG1.pin2
  N31: DRIVER.pin17, TRIG2.pin2
  N32: DRIVER.pin18, TRIG3.pin2
  N33: 10kΩ.Pin_0, Teensy1.D25, HCTL_RESET.Pin_3, HCTL_RESET.Pin_4
  N34: 10kΩ_2.Pin_0, Teensy1.D26, CNT_RESET.Pin_3, CNT_RESET.Pin_4
  N35: STAT_LED1.pin2, 80Ω.Pin_0
  N36: 80Ω.Pin_1, Teensy1.D27
  N37: 80Ω_2.Pin_0, STAT_LED2.pin2
  N38: 80Ω_2.Pin_1, Teensy1.D28
  N39: 80Ω_3.Pin_0, STAT_LED3.pin2
  N40: 80Ω_3.Pin_1, Teensy1.D29
  N41: 80Ω_4.Pin_0, STAT_LED4.pin2
  N42: 80Ω_4.Pin_1, Teensy1.D30
  N43: J2.pin1, Teensy1.A22/DAC1
  N44: J2.pin2, Teensy1.A21/DAC0
  N45: J2.pin3, Teensy1.D39
  N46: J2.pin4, Teensy1.D38
  N47: J2.pin5, Teensy1.D37
  N48: J2.pin6, Teensy1.D36
  N49: J2.pin7, Teensy1.D35
  N50: J2.pin8, Teensy1.D34
  N51: J2.pin9, Teensy1.D33
  N52: A9.pin2, Teensy1.A9/D23
  N53: A8.pin2, Teensy1.A8/D22
  N54: A3.pin2, Teensy1.A3/D17
  N55: A2.pin2, Teensy1.A2/D16

notes:
  quad_decoder_01
  JR 2019 UZH
  A+ brown
  B+ white
  B- blue
  A- green
  brown
  GND gray
  I+ yell.
  I- pink
  +5V red

custom parts:
  DIP - 16 pins: A DIP stand-in part for whatever IC you want. With 16 pins on a 300mil dual inline package (DIP) footprint.
  Teensy 3.6 (Basic): The Teensy is a complete USB-based microcontoller development system, in a very small footprint, capable of implementing many types of projects. All programming is done via the USB port. No special programmer is needed, only a standard micro-USB cable and a PC or Macintosh with a USB port.
